// Logisim project HX.circ as structural Verilog: 1 circuit, main circuit main
module main (
  input  D0,
  input  D1,
  input  D2,
  input  D3,
  input  K0,
  input  D4,
  input  K1,
  input  D5,
  input  K2,
  input  K3,
  input  D6,
  input  D7,
  input  K4,
  input  K5,
  input  K6,
  input  K7,
  output C0,
  output C1,
  output C2,
  output C3,
  output C4,
  output C5,
  output C6,
  output C7
);

  xor xor_1 (C0, D0, K0);
  xor xor_2 (C1, D1, K1);
  xor xor_3 (C2, D2, K2);
  xor xor_4 (C3, D3, K3);
  xor xor_5 (C4, D4, K4);
  xor xor_6 (C5, D5, K5);
  xor xor_7 (C6, D6, K6);
  xor xor_8 (C7, D7, K7);
endmodule
